# Fritzing sketch PiDAR_2.0.2 (saved by Fritzing 1.0.2b)
circuit board: 8.46667cm x 5.64444cm
breadboards: 1

parts:
  Mod1 = Raspberry Pi 4B
  A4988 = Pololu A4988 [package=SO16]
  Stepper = Stepper Motor - Bipolar
  M1 = LDRobot LD19 Lidar [package=THT]
  U1 = Intenso XS10000 [package=XS10000]
  R2 = Resistor [tolerance=±5% power=0.25W resistance=220 package=THT]
  R1 = Resistor [tolerance=±5% power=0.25W resistance=220 package=THT]
  Scan_Button = Momentary Switch [package=ksa_sealed_tac_switch]
  Power_Button = Momentary Switch [package=ksa_sealed_tac_switch]
  Boost_Convertor2 = Boost Convertor [part_number=XL6009E1 package=THT]
  C2 = Electrolytic Capacitor [capacitance=2.2mF voltage=35V package="0605 [SMD, electrolytic]"]
  DS2Y-5-DC5V3 = DS2Y-5-DC5V [part_number=DS2Y-5-DC5V]

nets:
  N1: Mod1.5V, U1.+, C2.+, DS2Y-5-DC5V3.13_COM
  N2: Mod1.GPIO3, Power_Button.1, Power_Button.2
  N3: Mod1.GND, A4988.GND#8, M1.pin3, U1.-, R2.Pin_1, R1.Pin_1, Boost_Convertor2.Negative_Input, C2.-, DS2Y-5-DC5V3.1_+
  N4: Mod1.GPIO15, M1.pin1
  N5: Mod1.GPIO17, Scan_Button.1, Scan_Button.2
  N6: Mod1.GPIO18, M1.pin2
  N7: Mod1.GPIO24, DS2Y-5-DC5V3.16_-
  N8: Mod1.ID_SD, Mod1.GPIO5, A4988.MS1
  N9: Mod1.GPIO6, A4988.MS2
  N10: Mod1.GPIO13, A4988.MS3
  N11: Mod1.GPIO19, A4988.STEP
  N12: Mod1.GPIO26, A4988.DIR
  N13: A4988.RESET, A4988.SLEEP
  N14: A4988.VDD, M1.pin4, Boost_Convertor2.Positive_Input, DS2Y-5-DC5V3.9_N.O.
  N15: A4988.1B, Stepper.B-
  N16: A4988.1A, Stepper.B+
  N17: A4988.2A, Stepper.A+
  N18: A4988.2B, Stepper.A-
  N19: A4988.GND#14, Boost_Convertor2.Negative_Output
  N20: A4988.VMOT, Boost_Convertor2.Positive_Output
  N21: R2.Pin_0, Power_Button.3, Power_Button.4
  N22: R1.Pin_0, Scan_Button.3, Scan_Button.4

custom parts:
  Stepper Motor - Bipolar: Simple, but very powerful bi polar stepper motor. 4 wire
  Intenso XS10000: 10000mAh Powerbank 91 x 63 x 22 mm 182 g
  Boost Convertor: DC to DC boost convertor
